// Logisim project MIPS 4-bit CPU.circ as structural Verilog: 1 circuit, main circuit 4-bit CPU
module _4_bit_CPU (
  input  [3:0] in_1,
  input  PCSrc_J,
  input  PCSrc_beq
);

  wire and_1_out, Clk_out, mips_alu_4_bit_1_p3, mips_alu_4_bit_1_p4, undriven, undriven_2, undriven_3,
       undriven_4, undriven_5, undriven_6;
  wire [3:0] adder_1_p4, adder_2_p1, adder_2_p2, adder_2_p5, mips_alu_4_bit_1_p5, multiplexer_1_out,
       multiplexer_2_out, multiplexer_3_out, multiplexer_4_out, multiplexer_5_out, PC_q, ram_1_data,
       registerfile_1_r1_data, registerfile_1_r2_data;

  Register #(.width(4)) PC (.D(multiplexer_1_out), .Q(PC_q), .clk(Clk_out));  // open: en, clr
  Clock Clk (.out(Clk_out));
  // Adder adder_1: pin names not known; wires that end beside it: PC_q, 4'b0001, PC_q, adder_1_p4
  Multiplexer #(.width(4), .disabled(0), .enable("false")) multiplexer_1 (
    .in0(multiplexer_3_out), .in1(in_1), .out(multiplexer_1_out), .sel(PCSrc_J));
  // Adder adder_2: pin names not known; wires that end beside it: adder_2_p1, adder_2_p2, adder_1_p4, in_1, adder_2_p5
  and and_1 (and_1_out, mips_alu_4_bit_1_p4, PCSrc_beq);
  Multiplexer #(.width(4), .disabled(0), .enable("false")) multiplexer_2 (
    .in0(adder_2_p2), .in1(in_1), .out(multiplexer_2_out), .sel(undriven));
  Multiplexer #(.width(4), .disabled(0), .enable("false")) multiplexer_3 (
    .in0(adder_1_p4), .in1(adder_2_p5), .out(multiplexer_3_out), .sel(and_1_out));
  RegisterFile registerfile_1 (
    .Write_Data(multiplexer_5_out), .RegWrite(undriven_2), .Write_num(multiplexer_2_out),
    .R1_Data(registerfile_1_r1_data), .R2_Data(registerfile_1_r2_data), .R1_num(adder_2_p1),
    .R2_num(adder_2_p2));  // open: Clk
  Multiplexer #(.width(4), .disabled(0), .enable("false")) multiplexer_4 (
    .in0(registerfile_1_r2_data), .in1(in_1), .out(multiplexer_4_out), .sel(undriven_3));
  // MIPS_ALU_4_bit mips_alu_4_bit_1: pin names not known; wires that end beside it: registerfile_1_r1_data, multiplexer_4_out, mips_alu_4_bit_1_p3, mips_alu_4_bit_1_p4, mips_alu_4_bit_1_p5
  RAM #(.addrWidth(4), .dataWidth(4), .bus("separate")) ram_1 (
    .addr(mips_alu_4_bit_1_p5), .din(registerfile_1_r2_data), .data(ram_1_data), .str(undriven_4),
    .ld(undriven_5));  // open: sel, clk, clr
  Multiplexer #(.width(4), .disabled(0), .enable("false")) multiplexer_5 (
    .in0(mips_alu_4_bit_1_p5), .in1(ram_1_data), .out(multiplexer_5_out), .sel(undriven_6));

  // Notes on the sheet:
  //   writeDest
  //             RegWriteEN
  //        ALUSrc
  //   ALUOp
  //          MemWrite
  //   MemRead
  //         w.val.src
endmodule
